# Fritzing sketch PCB final design (saved by Fritzing 1.0.5)
circuit board: 15.8607cm x 9.90846cm
breadboards: 1

parts:
  VR1 = LM2596 (TO263) [part_number=LM2596 package=TO263]
  J1 = XT60 Connector [package=THT]
  nano_GND = Header 1 [package=smtso-256-et]
  nano_5V = Header 1 [package=smtso-256-et]
  IR5 = JST-VHR-3N [part_number=JST-VHR-3N package=THT]
  A5 = Header 1 [package=smtso-256-et]
  A6 = Header 1 [package=smtso-256-et]
  A7 = Header 1 [package=smtso-256-et]
  D2 = Header 1 [package=smtso-256-et]
  D3 = Header 1 [package=smtso-256-et]
  A1 = Header 1 [package=smtso-256-et]
  A4 = Header 1 [package=smtso-256-et]
  A2 = Header 1 [package=smtso-256-et]
  A3 = Header 1 [package=smtso-256-et]
  A0 = Header 1 [package=smtso-256-et]
  IR1 = JST-VHR-3N [part_number=JST-VHR-3N package=THT]
  IR2 = JST-VHR-3N [part_number=JST-VHR-3N package=THT]
  IR3 = JST-VHR-3N [part_number=JST-VHR-3N package=THT]
  IR4 = JST-VHR-3N [part_number=JST-VHR-3N package=THT]
  IR6 = JST-VHR-3N [part_number=JST-VHR-3N package=THT]
  IR7 = JST-VHR-3N [part_number=JST-VHR-3N package=THT]
  IR8 = JST-VHR-3N [part_number=JST-VHR-3N package=THT]
  IR9 = JST-VHR-3N [part_number=JST-VHR-3N package=THT]
  IR10 = JST-VHR-3N [part_number=JST-VHR-3N package=THT]
  block_terminal_(motors) = Camdenboss CTB0158-6 [part_number=CTB0158-6 package=THT]
  D5 = Header 1 [package=smtso-256-et]
  D6 = Header 1 [package=smtso-256-et]
  D7 = Header 1 [package=smtso-256-et]
  D8 = Header 1 [package=smtso-256-et]
  D9 = Header 1 [package=smtso-256-et]
  D10 = Header 1 [package=smtso-256-et]

nets:
  N1: VR1.Pin_1, J1.VCC, nano_5V.1
  N2: VR1.Pin_2, IR5.pin3, IR5.pin_6, IR1.pin3, IR1.pin_6, IR2.pin3, IR2.pin_6, IR3.pin3, IR3.pin_6, IR4.pin3, IR4.pin_6, IR6.pin3, IR6.pin_6, IR7.pin3, IR7.pin_6, IR8.pin3, IR8.pin_6, IR9.pin3, IR9.pin_6, IR10.pin3, IR10.pin_6
  N3: VR1.Pin_3, VR1.Tab, J1.GND, nano_GND.1, IR5.pin2, IR5.pin_5, IR1.pin2, IR1.pin_5, IR2.pin2, IR2.pin_5, IR3.pin2, IR3.pin_5, IR4.pin2, IR4.pin_5, IR6.pin2, IR6.pin_5, IR7.pin2, IR7.pin_5, IR8.pin2, IR8.pin_5, IR9.pin2, IR9.pin_5, IR10.pin2, IR10.pin_5
  N4: IR5.pin1, A4.1
  N5: A5.1, IR8.pin1, IR8.pin_4
  N6: A6.1, IR10.pin1, IR10.pin_4
  N7: A7.1, IR7.pin1, IR7.pin_4
  N8: D2.1, IR9.pin1, IR9.pin_4
  N9: D3.1, IR6.pin1
  N10: A1.1, IR2.pin1
  N11: A2.1, IR3.pin1, IR3.pin_4
  N12: A3.1, IR4.pin1, IR4.pin_4
  N13: A0.1, IR1.pin1, IR1.pin_4
  N14: block_terminal_(motors).pin1, D10.1
  N15: block_terminal_(motors).pin2, D9.1
  N16: block_terminal_(motors).pin3, D8.1
  N17: block_terminal_(motors).pin4, D7.1
  N18: block_terminal_(motors).pin5, D6.1
  N19: block_terminal_(motors).pin6, D5.1

custom parts:
  XT60 Connector: Yellow XT60 connector for high current loads up to 40A
