# Fritzing sketch main circuit (saved by Fritzing 1.0.5)
# 18650 Li-ion Battery: CC-BY Dr Kristofer Chan, King's College London/Remote-research.org
breadboards: 1

parts:
  buck_converter = LM2596 (TO263) [part_number=LM2596 package=TO263]
  microcontroller = Arduino Nano (Rev3.0)
  J1 = XT60 Connector [package=THT]
  BAT1 = 18650 Li-ion Battery [package=battery-18650]
  BAT2 = 18650 Li-ion Battery [package=battery-18650]
  BAT3 = 18650 Li-ion Battery [package=battery-18650]
  BAT4 = 18650 Li-ion Battery [package=battery-18650]
  BAT5 = 18650 Li-ion Battery [package=battery-18650]

nets:
  N1: buck_converter.Pin_1, BAT5.+
  N2: buck_converter.Pin_2, microcontroller.5V
  N3: buck_converter.Pin_3, buck_converter.Tab, microcontroller.GND, BAT5.-
  N4: J1.GND, BAT1.-, BAT2.-
  N5: J1.VCC, BAT3.+, BAT4.+
  N6: BAT1.+, BAT3.-
  N7: BAT2.+, BAT4.-

custom parts:
  XT60 Connector: Yellow XT60 connector for high current loads up to 40A
  18650 Li-ion Battery: 18650 li-ion Battery Standard 18650 battery with interactive connectors Creative Common Attribution 4.0 International (CC-BY 4.0) license. Any use of this part requires attribution of Dr Kristofer Chan, Department of Geography, King's College London. Contact kristofer.chan [at] kcl.ac.uk OR kris [at] remote-research.org for further information.
