# Fritzing sketch sensors (saved by Fritzing 1.0.5)
breadboards: 1

parts:
  IR2 = Infrared Proximity Sensor [distance_to_obstacle=50%]
  IR3 = Infrared Proximity Sensor [distance_to_obstacle=50%]
  IR4 = Infrared Proximity Sensor [distance_to_obstacle=50%]
  IR5 = Infrared Proximity Sensor [distance_to_obstacle=50%]
  IR1 = Infrared Proximity Sensor [distance_to_obstacle=50%]
  J1 = JST-03JQ-BT [part_number=JST-JQ-BT package=THT]
  J3 = JST-VHR-3N [part_number=JST-VHR-3N package=THT]
  J4 = JST-03JQ-BT [part_number=JST-JQ-BT package=THT]
  J5 = JST-VHR-3N [part_number=JST-VHR-3N package=THT]
  J6 = JST-03JQ-BT [part_number=JST-JQ-BT package=THT]
  J7 = JST-VHR-3N [part_number=JST-VHR-3N package=THT]
  J8 = JST-03JQ-BT [part_number=JST-JQ-BT package=THT]
  J9 = JST-VHR-3N [part_number=JST-VHR-3N package=THT]
  J10 = JST-03JQ-BT [part_number=JST-JQ-BT package=THT]
  J11 = JST-VHR-3N [part_number=JST-VHR-3N package=THT]

nets:
  N1: IR2.Vout, J8.pin2, J9.pin2, J9.pin_5
  N2: IR2.GND, J8.pin3, J9.pin3, J9.pin_6
  N3: IR2.Vcc, J8.pin1, J9.pin1, J9.pin_4
  N4: IR3.Vout, J6.pin2, J7.pin2
  N5: IR3.GND, J6.pin3, J7.pin3
  N6: IR3.Vcc, J6.pin1, J7.pin1, J7.pin_4
  N7: IR4.Vout, J4.pin2, J5.pin2
  N8: IR4.GND, J4.pin3, J5.pin3
  N9: IR4.Vcc, J4.pin1, J5.pin1
  N10: IR5.Vout, J1.pin2, J3.pin2
  N11: IR5.GND, J1.pin3, J3.pin3, J3.pin_6
  N12: IR5.Vcc, J1.pin1, J3.pin1
  N13: IR1.Vout, J10.pin2, J11.pin2
  N14: IR1.GND, J10.pin3, J11.pin3
  N15: IR1.Vcc, J10.pin1, J11.pin1
